// Logisim project new.circ as structural Verilog: 7 circuits, main circuit Snake
module Proc (
);

  wire cdm_8_mark5_1_p1, cdm_8_mark5_1_p2, cdm_8_mark5_1_p4, cdm_8_mark5_1_p5, cdm_8_mark5_1_p6,
       cdm_8_mark5_1_p7, cdm_8_mark5_1_p8, CI, code, data, I_Osel, in_out_prime, mem, nand_1_out, not_1_out,
       not_2_out, RAM;
  wire [3:0] I_Oadr;
  wire [7:0] cdm_8_mark5_1_p12, cdm_8_mark5_1_p13, I_Odat;
  wire [7:4] cdm_8_mark5_1_p11;

  // Probe on cdm_8_mark5_1_p5
  // Probe on cdm_8_mark5_1_p4
  // Probe on cdm_8_mark5_1_p2
  // Probe on cdm_8_mark5_1_p1
  // Probe on cdm_8_mark5_1_p7
  // Probe on cdm_8_mark5_1_p6
  Clock clock_1 (.out(CI));
  and and_1 (I_Osel, not_2_out, CI, data);
  Decoder decoder_1 (.out0(code), .out1(data), .sel(cdm_8_mark5_1_p8), .en(mem));
  // CdM_8_mark5 cdm_8_mark5_1: pin names not known; wires that end beside it: cdm_8_mark5_1_p1, cdm_8_mark5_1_p2, CI, cdm_8_mark5_1_p4, cdm_8_mark5_1_p5, cdm_8_mark5_1_p6, cdm_8_mark5_1_p7, cdm_8_mark5_1_p8, mem, in_out_prime, {cdm_8_mark5_1_p11, I_Oadr}, cdm_8_mark5_1_p12, cdm_8_mark5_1_p13
  not not_1 (not_1_out, in_out_prime);
  assign cdm_8_mark5_1_p13 = in_out_prime ? I_Odat : 8'bz;  // Controlled_Buffer controlled_buffer_1
  not not_2 (not_2_out, nand_1_out);
  and and_2 (RAM, nand_1_out, data);
  assign I_Odat = not_1_out ? cdm_8_mark5_1_p12 : 8'bz;  // Controlled_Buffer controlled_buffer_2
  nand nand_1 (nand_1_out, cdm_8_mark5_1_p11[4], cdm_8_mark5_1_p11[5], cdm_8_mark5_1_p11[6], cdm_8_mark5_1_p11[7]);
  ROM rom_1 (.addr({cdm_8_mark5_1_p11, I_Oadr}), .data(I_Odat), .sel(code));
  RAM ram_1 (.addr({cdm_8_mark5_1_p11, I_Oadr}), .data(I_Odat), .sel(RAM), .clk(CI), .ld(in_out_prime));  // open: clr

  // Other names for the same wires on the sheet: rd_wr_prime = in_out_prime
endmodule

module Head (
  input  Clock,
  input  W,
  input  A,
  input  S,
  input  D,
  output [31:0] _0,
  output [31:0] out_7,
  output [31:0] out_8,
  output [31:0] out_9,
  output [31:0] out_10,
  output [31:0] out_11,
  output [31:0] out_12,
  output [31:0] out_13,
  output [31:0] out_14,
  output [31:0] out_15,
  output [31:0] out_16,
  output [31:0] out_17,
  output [31:0] out_18,
  output [31:0] out_19,
  output [31:0] out_20,
  output [31:0] out_21,
  output [31:0] out_22,
  output [31:0] out_23,
  output [31:0] out_24,
  output [31:0] out_25,
  output [31:0] out_26,
  output [31:0] out_27,
  output [31:0] out_28,
  output [31:0] out_29,
  output [31:0] out_30,
  output [31:0] out_31,
  output [31:0] out_32,
  output [31:0] out_33,
  output [31:0] out_34,
  output [31:0] out_35,
  output [31:0] out_36,
  output [31:0] out_37
);

  wire and_1_out, and_2_out, and_3_out, and_4_out, Clock_t, decoder_1_out0, decoder_1_out1, decoder_1_out2,
       decoder_1_out3, decoder_1_out4, decoder_1_out5, decoder_1_out6, decoder_1_out7, decoder_1_out8,
       decoder_1_out9, decoder_1_out10, decoder_1_out11, decoder_1_out12, decoder_1_out13, decoder_1_out14,
       decoder_1_out15, decoder_1_out16, decoder_1_out17, decoder_1_out18, decoder_1_out19, decoder_1_out20,
       decoder_1_out21, decoder_1_out22, decoder_1_out23, decoder_1_out24, decoder_1_out25, decoder_1_out26,
       decoder_1_out27, decoder_1_out28, decoder_1_out29, decoder_1_out30, decoder_1_out31, Down, Left,
       or_1_out, or_2_out, or_3_out, or_4_out, or_5_out, or_6_out, or_7_out, pull_resistor_2_node,
       pull_resistor_3_node, Right, Up;
  wire [4:0] counter_1_q, counter_2_q;

  Transistor #(.\type ("n"), .gate("br")) transistor_1 (.in(Clock), .out(Clock_t), .gate(or_1_out));
  Pull_Resistor pull_resistor_1 (.node(Clock_t));
  or or_1 (or_1_out, Up, Down, Left, Right);
  D_Flip_Flop d_ff_1 (.Q(Up), .preset(and_1_out), .reset(or_2_out));  // open: clk, D, Qn, en
  or or_2 (or_2_out, D, A);
  and and_1 (and_1_out, ~Down, W);  // AND_Gate
  D_Flip_Flop d_ff_2 (.Q(Down), .preset(and_2_out), .reset(or_3_out));  // open: clk, D, Qn, en
  or or_3 (or_3_out, D, A);
  and and_2 (and_2_out, ~Up, S);  // AND_Gate
  D_Flip_Flop d_ff_3 (.Q(Left), .preset(and_3_out), .reset(or_4_out));  // open: clk, D, Qn, en
  or or_4 (or_4_out, S, W);
  and and_3 (and_3_out, ~Right, A);  // AND_Gate
  D_Flip_Flop d_ff_4 (.Q(Right), .preset(and_4_out), .reset(or_5_out));  // open: clk, D, Qn, en
  and and_4 (and_4_out, ~Left, D);  // AND_Gate
  or or_5 (or_5_out, S, W);
  Counter #(.width(5), .max('h1f)) counter_1 (
    .load(Down), .Q(counter_1_q), .clk(pull_resistor_2_node));  // open: D, count, carry, clr
  Pull_Resistor pull_resistor_2 (.node(pull_resistor_2_node));
  Transistor transistor_2 (.in(Clock_t), .out(pull_resistor_2_node), .gate(or_6_out));
  or or_6 (or_6_out, Right, Left);
  Counter #(.width(5), .max('h1f)) counter_2 (
    .load(Left), .Q(counter_2_q), .clk(pull_resistor_3_node));  // open: D, count, carry, clr
  Pull_Resistor pull_resistor_3 (.node(pull_resistor_3_node));
  Transistor transistor_3 (.in(Clock_t), .out(pull_resistor_3_node), .gate(or_7_out));
  or or_7 (or_7_out, Up, Down);
  Decoder #(.select(5)) decoder_1 (
    .out0(decoder_1_out0), .out1(decoder_1_out1), .out2(decoder_1_out2), .out3(decoder_1_out3),
    .out4(decoder_1_out4), .out5(decoder_1_out5), .out6(decoder_1_out6), .out7(decoder_1_out7),
    .out8(decoder_1_out8), .out9(decoder_1_out9), .out10(decoder_1_out10), .out11(decoder_1_out11),
    .out12(decoder_1_out12), .out13(decoder_1_out13), .out14(decoder_1_out14), .out15(decoder_1_out15),
    .out16(decoder_1_out16), .out17(decoder_1_out17), .out18(decoder_1_out18), .out19(decoder_1_out19),
    .out20(decoder_1_out20), .out21(decoder_1_out21), .out22(decoder_1_out22), .out23(decoder_1_out23),
    .out24(decoder_1_out24), .out25(decoder_1_out25), .out26(decoder_1_out26), .out27(decoder_1_out27),
    .out28(decoder_1_out28), .out29(decoder_1_out29), .out30(decoder_1_out30), .out31(decoder_1_out31),
    .sel(counter_1_q));  // open: en
  go_line go_line_1 (.Out(out_7), .in_1(decoder_1_out1), .In(counter_2_q));
  go_line go_line_2 (.Out(_0), .in_1(decoder_1_out0), .In(counter_2_q));
  go_line go_line_3 (.Out(out_8), .in_1(decoder_1_out2), .In(counter_2_q));
  go_line go_line_4 (.Out(out_10), .in_1(decoder_1_out4), .In(counter_2_q));
  go_line go_line_5 (.Out(out_11), .in_1(decoder_1_out5), .In(counter_2_q));
  go_line go_line_6 (.Out(out_9), .in_1(decoder_1_out3), .In(counter_2_q));
  go_line go_line_7 (.Out(out_14), .in_1(decoder_1_out8), .In(counter_2_q));
  go_line go_line_8 (.Out(out_12), .in_1(decoder_1_out6), .In(counter_2_q));
  go_line go_line_9 (.Out(out_15), .in_1(decoder_1_out9), .In(counter_2_q));
  go_line go_line_10 (.Out(out_13), .in_1(decoder_1_out7), .In(counter_2_q));
  go_line go_line_11 (.Out(out_19), .in_1(decoder_1_out13), .In(counter_2_q));
  go_line go_line_12 (.Out(out_16), .in_1(decoder_1_out10), .In(counter_2_q));
  go_line go_line_13 (.Out(out_18), .in_1(decoder_1_out12), .In(counter_2_q));
  go_line go_line_14 (.Out(out_17), .in_1(decoder_1_out11), .In(counter_2_q));
  go_line go_line_15 (.Out(out_20), .in_1(decoder_1_out14), .In(counter_2_q));
  go_line go_line_16 (.Out(out_22), .in_1(decoder_1_out16), .In(counter_2_q));
  go_line go_line_17 (.Out(out_21), .in_1(decoder_1_out15), .In(counter_2_q));
  go_line go_line_18 (.Out(out_23), .in_1(decoder_1_out17), .In(counter_2_q));
  go_line go_line_19 (.Out(out_24), .in_1(decoder_1_out18), .In(counter_2_q));
  go_line go_line_20 (.Out(out_27), .in_1(decoder_1_out21), .In(counter_2_q));
  go_line go_line_21 (.Out(out_25), .in_1(decoder_1_out19), .In(counter_2_q));
  go_line go_line_22 (.Out(out_26), .in_1(decoder_1_out20), .In(counter_2_q));
  go_line go_line_23 (.Out(out_29), .in_1(decoder_1_out23), .In(counter_2_q));
  go_line go_line_24 (.Out(out_30), .in_1(decoder_1_out24), .In(counter_2_q));
  go_line go_line_25 (.Out(out_28), .in_1(decoder_1_out22), .In(counter_2_q));
  go_line go_line_26 (.Out(out_31), .in_1(decoder_1_out25), .In(counter_2_q));
  go_line go_line_27 (.Out(out_32), .in_1(decoder_1_out26), .In(counter_2_q));
  go_line go_line_28 (.Out(out_34), .in_1(decoder_1_out28), .In(counter_2_q));
  go_line go_line_29 (.Out(out_33), .in_1(decoder_1_out27), .In(counter_2_q));
  go_line go_line_30 (.Out(out_35), .in_1(decoder_1_out29), .In(counter_2_q));
  go_line go_line_31 (.Out(out_37), .in_1(decoder_1_out31), .In(counter_2_q));
  go_line go_line_32 (.Out(out_36), .in_1(decoder_1_out30), .In(counter_2_q));

  // Other names for the same wires on the sheet: Line_0[31:0] = _0; Line_1[31:0] = out_7; Line_2[31:0] = out_8;
  //   Line_3[31:0] = out_9; Line_4[31:0] = out_10; Line_5[31:0] = out_11; Line_6[31:0] = out_12;
  //   Line_7[31:0] = out_13; Line_8[31:0] = out_14; Line_9[31:0] = out_15; Line_10[31:0] = out_16;
  //   Line_11[31:0] = out_17; Line_12[31:0] = out_18; Line_13[31:0] = out_19; Line_14[31:0] = out_20;
  //   Line_15[31:0] = out_21; Line_16[31:0] = out_22; Line_17[31:0] = out_23; Line_18[31:0] = out_24;
  //   Line_19[31:0] = out_25; Line_20[31:0] = out_26; Line_21[31:0] = out_27; Line_22[31:0] = out_28;
  //   Line_23[31:0] = out_29; Line_24[31:0] = out_30; Line_25[31:0] = out_31; Line_26[31:0] = out_32;
  //   Line_27[31:0] = out_33; Line_28[31:0] = out_34; Line_29[31:0] = out_35; Line_30[31:0] = out_36;
  //   Line_31[31:0] = out_37
endmodule

module go_line (
  input  in_1,
  input  [4:0] In,
  output [31:0] Out
);

  wire [31:0] decoder_1_out31;

  Decoder #(.select(5)) decoder_1 (
    .out0(decoder_1_out31[31]), .out1(decoder_1_out31[30]), .out2(decoder_1_out31[29]),
    .out3(decoder_1_out31[28]), .out4(decoder_1_out31[27]), .out5(decoder_1_out31[26]),
    .out6(decoder_1_out31[25]), .out7(decoder_1_out31[24]), .out8(decoder_1_out31[23]),
    .out9(decoder_1_out31[22]), .out10(decoder_1_out31[21]), .out11(decoder_1_out31[20]),
    .out12(decoder_1_out31[19]), .out13(decoder_1_out31[18]), .out14(decoder_1_out31[17]),
    .out15(decoder_1_out31[16]), .out16(decoder_1_out31[15]), .out17(decoder_1_out31[14]),
    .out18(decoder_1_out31[13]), .out19(decoder_1_out31[12]), .out20(decoder_1_out31[11]),
    .out21(decoder_1_out31[10]), .out22(decoder_1_out31[9]), .out23(decoder_1_out31[8]),
    .out24(decoder_1_out31[7]), .out25(decoder_1_out31[6]), .out26(decoder_1_out31[5]),
    .out27(decoder_1_out31[4]), .out28(decoder_1_out31[3]), .out29(decoder_1_out31[2]),
    .out30(decoder_1_out31[1]), .out31(decoder_1_out31[0]), .sel(In));  // open: en
  Transistor #(.\type ("n"), .width(32)) transistor_1 (.in(decoder_1_out31), .out(Out), .gate(in_1));
  Pull_Resistor pull_resistor_1 (.node(Out));
endmodule

module to1bit (
  input  [6:0] In,
  output W,
  output A,
  output S,
  output D
);

  wire [6:0] xnor_1_out, xnor_2_out, xnor_3_out, xnor_4_out;

  assign xnor_1_out = ~(In ^ 7'b1110111);  // XNOR_Gate xnor_1, 7 bits wide
  assign xnor_2_out = ~(In ^ 7'b1100001);  // XNOR_Gate xnor_2, 7 bits wide
  assign xnor_3_out = ~(In ^ 7'b1110011);  // XNOR_Gate xnor_3, 7 bits wide
  assign xnor_4_out = ~(In ^ 7'b1100100);  // XNOR_Gate xnor_4, 7 bits wide
  and and_1 (W, xnor_1_out[0], xnor_1_out[1], xnor_1_out[2], xnor_1_out[3], xnor_1_out[4], xnor_1_out[5], xnor_1_out[6]);
  and and_2 (A, xnor_2_out[0], xnor_2_out[1], xnor_2_out[2], xnor_2_out[3], xnor_2_out[4], xnor_2_out[5], xnor_2_out[6]);
  and and_3 (S, xnor_3_out[0], xnor_3_out[1], xnor_3_out[2], xnor_3_out[3], xnor_3_out[4], xnor_3_out[5], xnor_3_out[6]);
  and and_4 (D, xnor_4_out[0], xnor_4_out[1], xnor_4_out[2], xnor_4_out[3], xnor_4_out[4], xnor_4_out[5], xnor_4_out[6]);
endmodule

module Pixel (
  input  Clock,
  input  [2:0] H,
  input  T,
  input  A,
  output Light,
  output Smash,
  output [1:0] Where
);

  wire and_1_out, and_2_out, and_3_out, or_1_out;

  or or_1 (or_1_out, and_1_out, and_3_out);
  and and_1 (and_1_out, H[2], ~Light);  // AND_Gate
  D_Flip_Flop #(.trigger("low")) d_ff_1 (
    .clk(Clock), .D(or_1_out), .Q(Light), .en(or_1_out), .reset(and_2_out));  // open: Qn, preset
  and and_2 (and_2_out, ~H[2], T);  // AND_Gate
  and and_3 (and_3_out, ~Light, A);  // AND_Gate
  Register #(.width(2)) register_1 (.D(H[1:0]), .Q(Where), .clk(H[2]), .clr(T));  // open: en
  and and_4 (Smash, Light, Clock, H[2]);

  // Other names for the same wires on the sheet: Where_t[1:0] = H[1:0]; H0 = H[2]

  // Notes on the sheet:
  //   H:
  //   T:
  //   A:
  //   Входные данные
  //   Clock:
  //    Вход тактового генератора
  //   1 - если координата хвоста совпадает с координатой пикселя
  //    1 - если координата яблока совпадает с координатой пикселя
  //   Датчик коллизии
  //   Как работает двух-битовый регистр Where:
  //   Запоминает движение головы для хвоста
  //   Последние два битика несут в себе текущее направление движения головы
  //   Включение пикселя(светодиода на матрице)
  //   Обновляет значение при вхождении головы(поднят бит H0)
  //   Очищает занчение при вхождении хвоста(поднят бит T)
  //    Массив битов, отвечающий за данные головы, первый бит(считая справа) поднят, если координата головы совпадает с этим пикселем
  //   Как работает D-тригер Light:
  //   И при этом сам бит Light не поднят
  //   Помимо этого, при помощи него определяется коллизия
  //   Это нужно, чтобы коллизия работала корректно, то есть
  //   LIght отвечает за то, горит ли данный пиксель на матрице или нет.
  //   Light поднимается когда либо поднят H0(голова зашла в этот битик), либо когда поднят бит A(здесь появилось яблочко)
  //   Однако, не всё так просто, к нему подключён Clock - тактовый генератор, Light поднимается только когда Clock = 0(срабатывает при низком уровне)
  //   Если изменять значение Light в тот же момент, когда на него подали H0, то Smash будет подниматься даже тогда, когда мы просто зажгли битик
  //   Light опускается если зашёл хвост, но при этом здесь нет головы, в этом случае коллизия не происходит, но и бит не должен опускаться
  //   Если же использовать тактовый генератор, то бит Smash будет подниматься только тогда, когда голова зашла в поднятый до этого битик(то что нужно!)
endmodule

module Line (
  input  EnA,
  input  EnT,
  input  [2:0] DataH,
  input  [4:0] Apple_X,
  input  [4:0] Tail_X,
  input  [4:0] Head_X,
  input  Clock,
  output [31:0] Out,
  output [1:0] Where,
  output Smash
);

  wire A0, A1, A2, A3, A4, A5, A6, A7, A8, A9, A10, A11, A12, A13, A14, A15, A16, A17, A18, A19, A20, A21,
       A22, A23, A24, A25, A26, A27, A28, A29, A30, A31, S0, S1, S2, S3, S4, S5, S6, S7, S8, S9, S10, S11,
       S12, S13, S14, S15, S16, S17, S18, S19, S20, S21, S22, S23, S24, S25, S26, S27, S28, S29, S30, S31,
       T0, T1, T2, T3, T4, T5, T6, T7, T8, T9, T10, T11, T12, T13, T14, T15, T16, T17, T18, T19, T20, T21,
       T22, T23, T24, T25, T26, T27, T28, T29, T30, T31;
  wire [1:0] W0, W1, W2, W3, W4, W5, W6, W7, W8, W9, W10, W11, W12, W13, W14, W15, W16, W17, W18, W19, W20,
       W21, W22, W23, W24, W25, W26, W27, W28, W29, W30, W31;
  wire [2:0] H0, H1, H2, H3, H4, H5, H6, H7, H8, H9, H10, H11, H12, H13, H14, H15, H16, H17, H18, H19, H20,
       H21, H22, H23, H24, H25, H26, H27, H28, H29, H30, H31;

  Pixel pixel_1 (.H(H0), .T(T0), .A(A0), .Light(Out[31]), .Smash(S0), .Where(W0), .Clock(Clock));
  Pixel pixel_2 (.H(H1), .T(T1), .A(A1), .Light(Out[30]), .Smash(S1), .Where(W1), .Clock(Clock));
  Pixel pixel_3 (.H(H16), .T(T16), .A(A16), .Light(Out[15]), .Smash(S16), .Where(W16), .Clock(Clock));
  Pixel pixel_4 (.H(H17), .T(T17), .A(A17), .Light(Out[14]), .Smash(S17), .Where(W17), .Clock(Clock));
  Demultiplexer #(.select(5)) demultiplexer_1 (
    .out0(A0), .out1(A1), .out2(A2), .out3(A3), .out4(A4), .out5(A5), .out6(A6), .out7(A7), .out8(A8),
    .out9(A9), .out10(A10), .out11(A11), .out12(A12), .out13(A13), .out14(A14), .out15(A15), .out16(A16),
    .out17(A17), .out18(A18), .out19(A19), .out20(A20), .out21(A21), .out22(A22), .out23(A23), .out24(A24),
    .out25(A25), .out26(A26), .out27(A27), .out28(A28), .out29(A29), .out30(A30), .out31(A31), .in(EnA),
    .sel(Apple_X));  // open: en
  Pixel pixel_5 (.H(H3), .T(T3), .A(A3), .Light(Out[28]), .Smash(S3), .Where(W3), .Clock(Clock));
  Pixel pixel_6 (.H(H2), .T(T2), .A(A2), .Light(Out[29]), .Smash(S2), .Where(W2), .Clock(Clock));
  Pixel pixel_7 (.H(H19), .T(T19), .A(A19), .Light(Out[12]), .Smash(S19), .Where(W19), .Clock(Clock));
  Pixel pixel_8 (.H(H18), .T(T18), .A(A18), .Light(Out[13]), .Smash(S18), .Where(W18), .Clock(Clock));
  Pixel pixel_9 (.H(H4), .T(T4), .A(A4), .Light(Out[27]), .Smash(S4), .Where(W4), .Clock(Clock));
  Pixel pixel_10 (.H(H5), .T(T5), .A(A5), .Light(Out[26]), .Smash(S5), .Where(W5), .Clock(Clock));
  Pixel pixel_11 (.H(H21), .T(T21), .A(A21), .Light(Out[10]), .Smash(S21), .Where(W21), .Clock(Clock));
  Pixel pixel_12 (.H(H20), .T(T20), .A(A20), .Light(Out[11]), .Smash(S20), .Where(W20), .Clock(Clock));
  Demultiplexer #(.select(5)) demultiplexer_2 (
    .out0(T0), .out1(T1), .out2(T2), .out3(T3), .out4(T4), .out5(T5), .out6(T6), .out7(T7), .out8(T8),
    .out9(T9), .out10(T10), .out11(T11), .out12(T12), .out13(T13), .out14(T14), .out15(T15), .out16(T16),
    .out17(T17), .out18(T18), .out19(T19), .out20(T20), .out21(T21), .out22(T22), .out23(T23), .out24(T24),
    .out25(T25), .out26(T26), .out27(T27), .out28(T28), .out29(T29), .out30(T30), .out31(T31), .in(EnT),
    .sel(Tail_X));  // open: en
  Pixel pixel_13 (.H(H6), .T(T6), .A(A6), .Light(Out[25]), .Smash(S6), .Where(W6), .Clock(Clock));
  Pixel pixel_14 (.H(H7), .T(T7), .A(A7), .Light(Out[24]), .Smash(S7), .Where(W7), .Clock(Clock));
  Pixel pixel_15 (.H(H23), .T(T23), .A(A23), .Light(Out[8]), .Smash(S23), .Where(W23), .Clock(Clock));
  Pixel pixel_16 (.H(H22), .T(T22), .A(A22), .Light(Out[9]), .Smash(S22), .Where(W22), .Clock(Clock));
  Pixel pixel_17 (.H(H9), .T(T9), .A(A9), .Light(Out[22]), .Smash(S9), .Where(W9), .Clock(Clock));
  Pixel pixel_18 (.H(H8), .T(T8), .A(A8), .Light(Out[23]), .Smash(S8), .Where(W8), .Clock(Clock));
  Pixel pixel_19 (.H(H25), .T(T25), .A(A25), .Light(Out[6]), .Smash(S25), .Where(W25), .Clock(Clock));
  Pixel pixel_20 (.H(H24), .T(T24), .A(A24), .Light(Out[7]), .Smash(S24), .Where(W24), .Clock(Clock));
  Demultiplexer #(.select(5), .width(3)) demultiplexer_3 (
    .out0(H0), .out1(H1), .out2(H2), .out3(H3), .out4(H4), .out5(H5), .out6(H6), .out7(H7), .out8(H8),
    .out9(H9), .out10(H10), .out11(H11), .out12(H12), .out13(H13), .out14(H14), .out15(H15), .out16(H16),
    .out17(H17), .out18(H18), .out19(H19), .out20(H20), .out21(H21), .out22(H22), .out23(H23), .out24(H24),
    .out25(H25), .out26(H26), .out27(H27), .out28(H28), .out29(H29), .out30(H30), .out31(H31), .in(DataH),
    .sel(Head_X));  // open: en
  Pixel pixel_21 (.H(H10), .T(T10), .A(A10), .Light(Out[21]), .Smash(S10), .Where(W10), .Clock(Clock));
  Pixel pixel_22 (.H(H11), .T(T11), .A(A11), .Light(Out[20]), .Smash(S11), .Where(W11), .Clock(Clock));
  Pixel pixel_23 (.H(H26), .T(T26), .A(A26), .Light(Out[5]), .Smash(S26), .Where(W26), .Clock(Clock));
  Pixel pixel_24 (.H(H27), .T(T27), .A(A27), .Light(Out[4]), .Smash(S27), .Where(W27), .Clock(Clock));
  Pixel pixel_25 (.H(H12), .T(T12), .A(A12), .Light(Out[19]), .Smash(S12), .Where(W12), .Clock(Clock));
  Pixel pixel_26 (.H(H13), .T(T13), .A(A13), .Light(Out[18]), .Smash(S13), .Where(W13), .Clock(Clock));
  Pixel pixel_27 (.H(H28), .T(T28), .A(A28), .Light(Out[3]), .Smash(S28), .Where(W28), .Clock(Clock));
  Pixel pixel_28 (.H(H29), .T(T29), .A(A29), .Light(Out[2]), .Smash(S29), .Where(W29), .Clock(Clock));
  Pixel pixel_29 (.H(H14), .T(T14), .A(A14), .Light(Out[17]), .Smash(S14), .Where(W14), .Clock(Clock));
  Pixel pixel_30 (.H(H15), .T(T15), .A(A15), .Light(Out[16]), .Smash(S15), .Where(W15), .Clock(Clock));
  Pixel pixel_31 (.H(H30), .T(T30), .A(A30), .Light(Out[1]), .Smash(S30), .Where(W30), .Clock(Clock));
  Pixel pixel_32 (.H(H31), .T(T31), .A(A31), .Light(Out[0]), .Smash(S31), .Where(W31), .Clock(Clock));
  or or_1 (Smash, S0, S1, S2, S3, S4, S5, S6, S7, S8, S9, S10, S11, S12, S13, S14, S15, S16, S17, S18, S19, S20, S21, S22, S23, S24, S25, S26, S27, S28, S29, S30, S31);
  Multiplexer #(.select(5), .width(2)) multiplexer_1 (
    .in0(W0), .in1(W1), .in2(W2), .in3(W3), .in4(W4), .in5(W5), .in6(W6), .in7(W7), .in8(W8), .in9(W9),
    .in10(W10), .in11(W11), .in12(W12), .in13(W13), .in14(W14), .in15(W15), .in16(W16), .in17(W17),
    .in18(W18), .in19(W19), .in20(W20), .in21(W21), .in22(W22), .in23(W23), .in24(W24), .in25(W25),
    .in26(W26), .in27(W27), .in28(W28), .in29(W29), .in30(W30), .in31(W31), .out(Where), .sel(Tail_X));  // open: en

  // Other names for the same wires on the sheet: L31 = Out[0]; L30 = Out[1]; L29 = Out[2]; L28 = Out[3]; L27 = Out[4];
  //   L26 = Out[5]; L25 = Out[6]; L24 = Out[7]; L23 = Out[8]; L22 = Out[9]; L21 = Out[10]; L20 = Out[11];
  //   L19 = Out[12]; L18 = Out[13]; L17 = Out[14]; L16 = Out[15]; L15 = Out[16]; L14 = Out[17]; L13 = Out[18];
  //   L12 = Out[19]; L11 = Out[20]; L10 = Out[21]; L9 = Out[22]; L8 = Out[23]; L7 = Out[24]; L6 = Out[25];
  //   L5 = Out[26]; L4 = Out[27]; L3 = Out[28]; L2 = Out[29]; L1 = Out[30]; L0 = Out[31]; Tail[4:0] = Tail_X

  // Notes on the sheet:
  //   Входные данные
  //   0
  //   31
  //   32 элемента Pixel
  //   Итоговые выходные данные всей строки
  //   Датчик коллизии
  //   Куда сдвигать хвост
  //   Значения светодиодов на линии
endmodule

module Snake (
);

  wire to1bit_1_a, to1bit_1_d, to1bit_1_s, to1bit_1_w;
  wire [6:0] keyboard_1_data;
  wire [31:0] head_1__0, head_1_out_7, head_1_out_8, head_1_out_9, head_1_out_10, head_1_out_11,
       head_1_out_12, head_1_out_13, head_1_out_14, head_1_out_15, head_1_out_16, head_1_out_17,
       head_1_out_18, head_1_out_19, head_1_out_20, head_1_out_21, head_1_out_22, head_1_out_23,
       head_1_out_24, head_1_out_25, head_1_out_26, head_1_out_27, head_1_out_28, head_1_out_29,
       head_1_out_30, head_1_out_31, head_1_out_32, head_1_out_33, head_1_out_34, head_1_out_35,
       head_1_out_36, head_1_out_37;

  Keyboard keyboard_1 (.data(keyboard_1_data));  // open: clk, re, clr, avail
  to1bit to1bit_1 (.W(to1bit_1_w), .A(to1bit_1_a), .S(to1bit_1_s), .D(to1bit_1_d), .In(keyboard_1_data));
  DotMatrix #(.inputtype("row"), .matrixcols(32), .matrixrows(32)) dotmatrix_1 (
    .row0(head_1_out_37), .row1(head_1_out_36), .row2(head_1_out_35), .row3(head_1_out_34),
    .row4(head_1_out_33), .row5(head_1_out_32), .row6(head_1_out_31), .row7(head_1_out_30),
    .row8(head_1_out_29), .row9(head_1_out_28), .row10(head_1_out_27), .row11(head_1_out_26),
    .row12(head_1_out_25), .row13(head_1_out_24), .row14(head_1_out_23), .row15(head_1_out_22),
    .row16(head_1_out_21), .row17(head_1_out_20), .row18(head_1_out_19), .row19(head_1_out_18),
    .row20(head_1_out_17), .row21(head_1_out_16), .row22(head_1_out_15), .row23(head_1_out_14),
    .row24(head_1_out_13), .row25(head_1_out_12), .row26(head_1_out_11), .row27(head_1_out_10),
    .row28(head_1_out_9), .row29(head_1_out_8), .row30(head_1_out_7), .row31(head_1__0));
  Head head_1 (
    ._0(head_1__0), .out_22(head_1_out_22), .out_7(head_1_out_7), .out_23(head_1_out_23),
    .out_8(head_1_out_8), .out_24(head_1_out_24), .out_9(head_1_out_9), .out_25(head_1_out_25),
    .out_10(head_1_out_10), .out_26(head_1_out_26), .out_11(head_1_out_11), .out_27(head_1_out_27),
    .out_12(head_1_out_12), .out_28(head_1_out_28), .out_13(head_1_out_13), .out_29(head_1_out_29),
    .out_14(head_1_out_14), .out_30(head_1_out_30), .out_15(head_1_out_15), .out_31(head_1_out_31),
    .out_16(head_1_out_16), .out_32(head_1_out_32), .out_17(head_1_out_17), .out_33(head_1_out_33),
    .out_18(head_1_out_18), .out_34(head_1_out_34), .out_19(head_1_out_19), .out_35(head_1_out_35),
    .out_20(head_1_out_20), .out_36(head_1_out_36), .out_21(head_1_out_21), .out_37(head_1_out_37),
    .W(to1bit_1_w), .A(to1bit_1_a), .S(to1bit_1_s), .D(to1bit_1_d));  // open: Clock

  // Notes on the sheet:
  //   Старый вариант
endmodule
