// Logisim project main.circ as structural Verilog: 11 circuits, main circuit Main
module Main (
  input  getApple
);

  wire A, AddPartToQ, and_1_out, and_4_out, and_6_out, and_7_out, and_8_out, and_10_out, and_11_out,
       BeatTail, cdm_8_mark5_1_p1, cdm_8_mark5_1_p2, cdm_8_mark5_1_p4, cdm_8_mark5_1_p5, cdm_8_mark5_1_p6,
       cdm_8_mark5_1_p7, CI, code, counter_1_carry, counter_4_carry, counter_6_carry, D, d_ff_2_q, data,
       decoder_3_out0, decoder_3_out1, DownT, EnG, EnK, GameClock, GameOver, GetScore, I_Oadr, I_Osel,
       in_out_prime, LeftT, LoadPartToTail, not_1_out, not_2_out, not_3_out, not_4_out, not_5_out, not_6_out,
       not_7_out, not_8_out, not_9_out, not_10_out, not_11_out, not_12_out, or_1_out, or_2_out, or_3_out,
       or_4_out, or_5_out, or_6_out, or_7_out, or_8_out, or_10_out, or_11_out, or_12_out, Pause, ProcGotPart,
       ProcWork, RAM, RightT, S, START, TailWait, Turn, UpT, W;
  wire [1:0] keyboard_2_where, register_3_q, Where;
  wire [4:0] CurrLength, CurrPart, head_1_head_x, head_1_head_y, Tail_X, Tail_Y, xnor_1_out, xnor_2_out;
  wire [6:0] controlled_buffer_1_out, keyboard_1_data;
  wire [6:5] and_13_out;
  wire [7:0] cdm_8_mark5_1_p10, cdm_8_mark5_1_p11, I_Odat, register_2_q;
  wire [7:1] cdm_8_mark5_1_p9;
  wire [31:0] tomatrix_1__0, tomatrix_1_out_10, tomatrix_1_out_11, tomatrix_1_out_12, tomatrix_1_out_13,
       tomatrix_1_out_14, tomatrix_1_out_15, tomatrix_1_out_16, tomatrix_1_out_17, tomatrix_1_out_18,
       tomatrix_1_out_19, tomatrix_1_out_20, tomatrix_1_out_21, tomatrix_1_out_22, tomatrix_1_out_23,
       tomatrix_1_out_24, tomatrix_1_out_25, tomatrix_1_out_26, tomatrix_1_out_27, tomatrix_1_out_28,
       tomatrix_1_out_29, tomatrix_1_out_30, tomatrix_1_out_31, tomatrix_1_out_32, tomatrix_1_out_33,
       tomatrix_1_out_34, tomatrix_1_out_35, tomatrix_1_out_36, tomatrix_1_out_37, tomatrix_1_out_38,
       tomatrix_1_out_39, tomatrix_1_out_40;

  Clock clock_1 (.out(CI));
  Keyboard_part #(.buflen(1)) keyboard_1 (.clk(CI), .clr(START), .data(keyboard_1_data));  // open: re, avail
  // Probe on cdm_8_mark5_1_p5
  // Probe on cdm_8_mark5_1_p4
  // Probe on cdm_8_mark5_1_p2
  // Probe on cdm_8_mark5_1_p1
  Counter #(.width(12), .max('h40)) counter_1 (
    .carry(counter_1_carry), .clk(CI), .clr(START));  // open: load, D, count, Q
  and and_1 (and_1_out, ~GameClock, EnK);  // AND_Gate
  // CdM_8_mark5 cdm_8_mark5_1: pin names not known; wires that end beside it: cdm_8_mark5_1_p1, cdm_8_mark5_1_p2, CI, cdm_8_mark5_1_p4, cdm_8_mark5_1_p5, cdm_8_mark5_1_p6, cdm_8_mark5_1_p7, in_out_prime, {cdm_8_mark5_1_p9, I_Oadr}, cdm_8_mark5_1_p10, cdm_8_mark5_1_p11
  and and_2 (GameClock, counter_1_carry, EnG, ~or_1_out);  // AND_Gate
  or or_1 (or_1_out, Pause, ProcWork, GameOver);
  assign controlled_buffer_1_out = and_1_out ? keyboard_1_data : 7'bz;  // Controlled_Buffer controlled_buffer_1
  Pull_Resistor pull_resistor_1 (.node(controlled_buffer_1_out));
  Keyboard keyboard_2 (
    .GameClock(GameClock), .Turn(Turn), .START(START), .Pause(Pause), .Where(keyboard_2_where), .W(W), .A(A),
    .S(S), .D(D), .In(controlled_buffer_1_out));
  Decoder #(.disabled(0)) decoder_1 (.out0(code), .out1(data), .sel(cdm_8_mark5_1_p6), .en(cdm_8_mark5_1_p7));
  assign I_Odat = not_1_out ? cdm_8_mark5_1_p10 : 8'bz;  // Controlled_Buffer controlled_buffer_2
  not not_1 (not_1_out, in_out_prime);
  assign cdm_8_mark5_1_p11 = in_out_prime ? I_Odat : 8'bz;  // Controlled_Buffer controlled_buffer_3
  Register #(.width(2), .trigger("falling")) register_1 (
    .D(keyboard_2_where), .Q(Where), .clk(Turn), .clr(START));  // open: en
  and and_3 (I_Osel, and_4_out, CI, data);
  or or_2 (or_2_out, DownT, START);
  not not_2 (not_2_out, START);
  and and_4 (and_4_out, ~cdm_8_mark5_1_p9[1], ~cdm_8_mark5_1_p9[2], ~cdm_8_mark5_1_p9[3], cdm_8_mark5_1_p9[4], cdm_8_mark5_1_p9[5], cdm_8_mark5_1_p9[6], cdm_8_mark5_1_p9[7]);  // AND_Gate
  and and_5 (RAM, data, ~I_Osel);  // AND_Gate
  Counter #(.width(5), .max('h1f)) counter_2 (
    .load(or_2_out), .D(5'b10000), .count(not_2_out), .Q(Tail_Y), .clk(or_3_out));  // open: carry, clr
  or or_3 (or_3_out, START, and_6_out);
  and and_6 (and_6_out, or_4_out, ~TailWait, GameClock);  // AND_Gate
  or or_4 (or_4_out, UpT, DownT);
  not not_3 (not_3_out, CI);
  ROM rom_1 (.addr({cdm_8_mark5_1_p9, I_Oadr}), .data(I_Odat), .sel(code));
  RAM ram_1 (
    .addr({cdm_8_mark5_1_p9, I_Oadr}), .data(I_Odat), .sel(RAM), .clk(not_3_out), .ld(in_out_prime));  // open: clr
  or or_5 (or_5_out, LeftT, START);
  Counter #(.width(5), .max('h1f)) counter_3 (
    .load(or_5_out), .D(5'b01111), .count(not_4_out), .Q(Tail_X), .clk(or_6_out));  // open: carry, clr
  not not_4 (not_4_out, START);
  or or_6 (or_6_out, START, and_7_out);
  and and_7 (and_7_out, or_7_out, ~TailWait, GameClock);  // AND_Gate
  or or_7 (or_7_out, LeftT, RightT);
  and and_8 (and_8_out, xnor_1_out[0], xnor_1_out[1], xnor_1_out[2], xnor_1_out[3], xnor_1_out[4]);
  and and_9 (GetScore, getApple, GameClock);
  Counter #(.width(5), .max('h1f)) counter_4 (
    .Q(CurrPart), .carry(counter_4_carry), .clk(GameClock), .clr(or_8_out));  // open: load, D, count
  or or_8 (or_8_out, not_5_out, START);
  assign xnor_1_out = ~(CurrPart ^ CurrLength);  // XNOR_Gate xnor_1, 5 bits wide
  D_Flip_Flop #(.trigger("falling")) d_ff_1 (
    .clk(GameClock), .D(GetScore), .Q(TailWait), .reset(START));  // open: Qn, preset, en
  D_Flip_Flop #(.trigger("falling")) d_ff_2 (.clk(START), .D(1'b1), .Q(d_ff_2_q), .reset(EnG));  // open: Qn, preset, en
  assign xnor_2_out = ~({5{1'b0}} ^ CurrPart);  // XNOR_Gate xnor_2, 5 bits wide
  or or_9 (AddPartToQ, and_8_out, counter_4_carry, Turn);
  not not_5 (not_5_out, not_6_out);
  not not_6 (not_6_out, AddPartToQ);
  not not_7 (not_7_out, START);
  toMatrix tomatrix_1 (
    .Head_X(head_1_head_x), .Tail_X(Tail_X), .Head_Y(head_1_head_y), .Tail_Y(Tail_Y), ._0(tomatrix_1__0),
    .out_25(tomatrix_1_out_25), .out_10(tomatrix_1_out_10), .out_26(tomatrix_1_out_26),
    .out_11(tomatrix_1_out_11), .out_27(tomatrix_1_out_27), .out_12(tomatrix_1_out_12),
    .out_28(tomatrix_1_out_28), .out_13(tomatrix_1_out_13), .out_29(tomatrix_1_out_29),
    .out_14(tomatrix_1_out_14), .out_30(tomatrix_1_out_30), .out_15(tomatrix_1_out_15),
    .out_31(tomatrix_1_out_31), .out_16(tomatrix_1_out_16), .out_32(tomatrix_1_out_32), .Smash(BeatTail),
    .out_17(tomatrix_1_out_17), .out_33(tomatrix_1_out_33), .out_18(tomatrix_1_out_18),
    .out_34(tomatrix_1_out_34), .out_19(tomatrix_1_out_19), .out_35(tomatrix_1_out_35),
    .out_20(tomatrix_1_out_20), .out_36(tomatrix_1_out_36), .out_21(tomatrix_1_out_21),
    .out_37(tomatrix_1_out_37), .out_22(tomatrix_1_out_22), .out_38(tomatrix_1_out_38),
    .out_23(tomatrix_1_out_23), .out_39(tomatrix_1_out_39), .out_24(tomatrix_1_out_24),
    .out_40(tomatrix_1_out_40), .En(EnG), .CLEAR(START), .START(d_ff_2_q));
  DotMatrix #(.inputtype("row"), .matrixcols(32), .matrixrows(32)) dotmatrix_1 (
    .row0(tomatrix_1_out_40), .row1(tomatrix_1_out_39), .row2(tomatrix_1_out_38), .row3(tomatrix_1_out_37),
    .row4(tomatrix_1_out_36), .row5(tomatrix_1_out_35), .row6(tomatrix_1_out_34), .row7(tomatrix_1_out_33),
    .row8(tomatrix_1_out_32), .row9(tomatrix_1_out_31), .row10(tomatrix_1_out_30), .row11(tomatrix_1_out_29),
    .row12(tomatrix_1_out_28), .row13(tomatrix_1_out_27), .row14(tomatrix_1_out_26),
    .row15(tomatrix_1_out_25), .row16(tomatrix_1_out_24), .row17(tomatrix_1_out_23),
    .row18(tomatrix_1_out_22), .row19(tomatrix_1_out_21), .row20(tomatrix_1_out_20),
    .row21(tomatrix_1_out_19), .row22(tomatrix_1_out_18), .row23(tomatrix_1_out_17),
    .row24(tomatrix_1_out_16), .row25(tomatrix_1_out_15), .row26(tomatrix_1_out_14),
    .row27(tomatrix_1_out_13), .row28(tomatrix_1_out_12), .row29(tomatrix_1_out_11),
    .row30(tomatrix_1_out_10), .row31(tomatrix_1__0));
  Head head_1 (
    .W(W), .A(A), .S(S), .D(D), .START(START), .GameClock(GameClock), .Head_Y(head_1_head_y),
    .Head_X(head_1_head_x), .Turn(Turn));
  nand nand_1 (EnK, xnor_2_out[0], xnor_2_out[1], xnor_2_out[2], xnor_2_out[3], xnor_2_out[4]);
  Counter #(.width(5), .max('h1f), .ongoal("stay")) counter_5 (
    .load(START), .D(5'b00100), .count(not_7_out), .Q(CurrLength), .clk(or_10_out));  // open: carry, clr
  or or_10 (or_10_out, START, GetScore);
  D_Flip_Flop d_ff_3 (.Q(GameOver), .preset(BeatTail), .reset(START));  // open: clk, D, Qn, en
  Button u_START (.out(START));
  not not_8 (not_8_out, not_9_out);
  not not_9 (not_9_out, START);
  assign I_Odat = ProcGotPart ? register_2_q : 8'bz;  // Controlled_Buffer controlled_buffer_4
  Register register_2 (.D({Where, 1'b0, CurrPart}), .Q(register_2_q), .clk(AddPartToQ), .clr(START));  // open: en
  not not_10 (not_10_out, LoadPartToTail);
  or or_11 (or_11_out, LoadPartToTail, and_10_out);
  D_Flip_Flop #(.trigger("falling")) d_ff_4 (
    .clk(not_8_out), .D(1'b1), .Q(EnG), .reset(GameOver));  // open: Qn, preset, en
  _7_Segment_Display u_7_segment_display_1 ();  // open: g, f, a, b, e, d, c, dp
  _7_Segment_Display u_7_segment_display_2 ();  // open: g, f, a, b, e, d, c, dp
  assign I_Odat = and_11_out ? {EnG, and_13_out, {5{1'b0}}} : 8'bz;  // Controlled_Buffer controlled_buffer_5
  D_Flip_Flop #(.trigger("falling")) d_ff_5 (
    .Q(and_13_out[6]), .preset(AddPartToQ), .reset(or_12_out));  // open: clk, D, Qn, en
  or or_12 (or_12_out, ProcGotPart, START);
  not not_11 (not_11_out, TailWait);
  Counter #(.width(5), .max('h1f), .ongoal("load")) counter_6 (
    .load(1'b1), .D(I_Odat[4:0]), .count(not_10_out), .carry(counter_6_carry), .clk(or_11_out), .clr(START));  // open: Q
  and and_10 (and_10_out, ~TailWait, GameClock);  // AND_Gate
  Register #(.width(2)) register_3 (.D(I_Odat[7:6]), .Q(register_3_q), .clk(LoadPartToTail), .clr(START));  // open: en
  and and_11 (and_11_out, decoder_3_out1, ~I_Oadr);  // AND_Gate
  and and_12 (ProcGotPart, decoder_3_out1, I_Oadr);
  or or_13 (ProcWork, and_13_out[6], and_13_out[5]);
  Decoder #(.select(2), .disabled(0)) decoder_2 (
    .out0(UpT), .out1(LeftT), .out2(DownT), .out3(RightT), .sel(register_3_q), .en(not_12_out));
  and and_13 (and_13_out[5], not_11_out, counter_6_carry);
  not not_12 (not_12_out, and_13_out[5]);
  Decoder #(.disabled(0)) decoder_3 (.out0(decoder_3_out0), .out1(decoder_3_out1), .sel(in_out_prime), .en(I_Osel));
  and and_14 (LoadPartToTail, I_Oadr, decoder_3_out0);

  // Other names for the same wires on the sheet: KeyboardClock = CI; rd_wr_prime = in_out_prime

  // Notes on the sheet:
  //   contents of rom_1 (hex, n*v repeats v):
  //   d0 f0 b1 5 e4 1f d0 0 d1 f2 a4 b5 d0 4 a4 d1 f3 d0 1 a4 d1 f4 d0 1 a4 d0 f0 b1 5 e5 1b 25 5 e5 42 d2
  //   f1 ba a e0 42 d0 f3 b0 a2 8c d2 f3 a8 8e b8 8c a8 d0 f3 b0 d2 f0 72 e1 42 d2 0 d0 f3 a2 25 5 e5 6b
  //   d0 f4 b0 0 e0 6b 88 d2 f4 a8 d0 f2 b0 b0 d2 f1 a8 d0 f2 b0 8c d2 f2 a8 d0 f2 b0 d2 f0 72 e1 6b d2 0
  //   d0 f2 a2 ee
endmodule

// TAIL
module Tail (
  input  EnT,
  input  GetScore,
  input  Clock,
  input  START,
  input  Up,
  input  Left,
  input  Down,
  input  Right,
  output [4:0] Tail_Y,
  output [4:0] Tail_X
);

  wire and_2_out, and_3_out, Clock_t, not_1_out, not_2_out, or_1_out, or_2_out, or_3_out, or_4_out, or_5_out,
       or_6_out;

  and and_1 (Clock_t, EnT, ~GetScore, Clock);  // AND_Gate
  or or_1 (or_1_out, Down, START);
  not not_1 (not_1_out, START);
  or or_2 (or_2_out, START, and_2_out);
  and and_2 (and_2_out, or_3_out, Clock_t);
  or or_3 (or_3_out, Up, Down);
  Counter #(.width(5), .max('h1f)) counter_1 (
    .load(or_1_out), .D(5'b01100), .count(not_1_out), .Q(Tail_Y), .clk(or_2_out));  // open: carry, clr
  or or_4 (or_4_out, Left, START);
  Counter #(.width(5), .max('h1f)) counter_2 (
    .load(or_4_out), .D(5'b01111), .count(not_2_out), .Q(Tail_X), .clk(or_5_out));  // open: carry, clr
  not not_2 (not_2_out, START);
  or or_5 (or_5_out, START, and_3_out);
  and and_3 (and_3_out, or_6_out, Clock_t);
  or or_6 (or_6_out, Left, Right);
endmodule

// HEAD
module Head (
  input  W,
  input  A,
  input  S,
  input  D,
  input  START,
  input  GameClock,
  output [4:0] Head_Y,
  output [4:0] Head_X,
  output Turn
);

  wire and_1_out, and_2_out, and_3_out, and_4_out, and_5_out, and_6_out, and_7_out, and_8_out, Down, Left,
       not_1_out, not_2_out, not_4_out, or_1_out, or_2_out, or_3_out, or_4_out, or_5_out, or_6_out, or_7_out,
       or_8_out, or_9_out, or_10_out, or_11_out, or_12_out, or_13_out, or_14_out, or_15_out, or_16_out,
       Right, Up;

  or or_1 (or_1_out, Down, START);
  not not_1 (not_1_out, START);
  or or_2 (or_2_out, START, and_1_out);
  or or_3 (or_3_out, Up, Down);
  Counter #(.width(5), .max('h1f)) counter_1 (
    .load(or_1_out), .D(5'b10100), .count(not_1_out), .Q(Head_Y), .clk(or_2_out));  // open: carry, clr
  and and_1 (and_1_out, or_3_out, GameClock);
  D_Flip_Flop d_ff_1 (.Q(Up), .preset(or_5_out), .reset(or_4_out));  // open: clk, D, Qn, en
  or or_4 (or_4_out, A, D);
  or or_5 (or_5_out, START, and_2_out);
  and and_2 (and_2_out, ~Down, W);  // AND_Gate
  and and_3 (and_3_out, ~Up, S);  // AND_Gate
  or or_6 (or_6_out, Left, START);
  Counter #(.width(5), .max('h1f)) counter_2 (
    .load(or_6_out), .D(5'b01111), .count(not_2_out), .Q(Head_X), .clk(or_7_out));  // open: carry, clr
  not not_2 (not_2_out, START);
  or or_7 (or_7_out, START, and_4_out);
  and and_4 (and_4_out, or_8_out, GameClock);
  or or_8 (or_8_out, Left, Right);
  D_Flip_Flop d_ff_2 (.Q(Down), .preset(and_3_out), .reset(or_9_out));  // open: clk, D, Qn, en
  or or_9 (or_9_out, A, START, D);
  and and_5 (and_5_out, ~Right, A);  // AND_Gate
  D_Flip_Flop d_ff_3 (.Q(Left), .preset(and_5_out), .reset(or_10_out));  // open: clk, D, Qn, en
  and and_6 (and_6_out, ~Left, D);  // AND_Gate
  or or_10 (or_10_out, W, START, S);
  D_Flip_Flop d_ff_4 (.Q(Right), .preset(and_6_out), .reset(or_11_out));  // open: clk, D, Qn, en
  or or_11 (or_11_out, W, START, S);
  or or_12 (or_12_out, Down, Up);
  or or_13 (or_13_out, A, D);
  or or_14 (or_14_out, Left, Right);
  or or_15 (or_15_out, W, S);
  and and_7 (and_7_out, or_12_out, or_13_out);
  or or_16 (or_16_out, and_7_out, and_8_out);
  and and_8 (and_8_out, or_14_out, or_15_out);
  not not_3 (Turn, not_4_out);
  not not_4 (not_4_out, or_16_out);
endmodule

module toMatrix (
  input  START,
  input  CLEAR,
  input  [4:0] Head_X,
  input  [4:0] Tail_X,
  input  En,
  input  [4:0] Head_Y,
  input  [4:0] Tail_Y,
  output Smash,
  output [31:0] _0,
  output [31:0] out_10,
  output [31:0] out_11,
  output [31:0] out_12,
  output [31:0] out_13,
  output [31:0] out_14,
  output [31:0] out_15,
  output [31:0] out_16,
  output [31:0] out_17,
  output [31:0] out_18,
  output [31:0] out_19,
  output [31:0] out_20,
  output [31:0] out_21,
  output [31:0] out_22,
  output [31:0] out_23,
  output [31:0] out_24,
  output [31:0] out_25,
  output [31:0] out_26,
  output [31:0] out_27,
  output [31:0] out_28,
  output [31:0] out_29,
  output [31:0] out_30,
  output [31:0] out_31,
  output [31:0] out_32,
  output [31:0] out_33,
  output [31:0] out_34,
  output [31:0] out_35,
  output [31:0] out_36,
  output [31:0] out_37,
  output [31:0] out_38,
  output [31:0] out_39,
  output [31:0] out_40
);

  wire decoder_1_out17, decoder_1_out18, decoder_1_out19, H0, H1, H2, H3, H4, H5, H6, H7, H8, H9, H10, H11,
       H12, H13, H14, H15, H16, H17, H18, H19, H20, H21, H22, H23, H24, H25, H26, H27, H28, H29, H30, H31,
       S0, S1, S2, S3, S4, S5, S6, S7, S8, S9, S10, S11, S12, S13, S14, S15, S16, S17, S18, S19, S20, S21,
       S22, S23, S24, S25, S26, S27, S28, S29, S30, S31, T0, T1, T2, T3, T4, T5, T6, T7, T8, T9, T10, T11,
       T12, T13, T14, T15, T16, T17, T18, T19, T20, T21, T22, T23, T24, T25, T26, T27, T28, T29, T30, T31;

  Decoder #(.select(5), .disabled(0)) decoder_1 (
    .out0(H0), .out1(H1), .out2(H2), .out3(H3), .out4(H4), .out5(H5), .out6(H6), .out7(H7), .out8(H8),
    .out9(H9), .out10(H10), .out11(H11), .out12(H12), .out13(H13), .out14(H14), .out15(H15), .out16(H16),
    .out17(decoder_1_out17), .out18(decoder_1_out18), .out19(decoder_1_out19), .out20(H20), .out21(H21),
    .out22(H22), .out23(H23), .out24(H24), .out25(H25), .out26(H26), .out27(H27), .out28(H28), .out29(H29),
    .out30(H30), .out31(H31), .sel(Head_Y), .en(En));
  or or_1 (H17, START, decoder_1_out17);
  or or_2 (H18, START, decoder_1_out18);
  or or_3 (H19, START, decoder_1_out19);
  Decoder #(.select(5), .disabled(0)) decoder_2 (
    .out0(T0), .out1(T1), .out2(T2), .out3(T3), .out4(T4), .out5(T5), .out6(T6), .out7(T7), .out8(T8),
    .out9(T9), .out10(T10), .out11(T11), .out12(T12), .out13(T13), .out14(T14), .out15(T15), .out16(T16),
    .out17(T17), .out18(T18), .out19(T19), .out20(T20), .out21(T21), .out22(T22), .out23(T23), .out24(T24),
    .out25(T25), .out26(T26), .out27(T27), .out28(T28), .out29(T29), .out30(T30), .out31(T31), .sel(Tail_Y),
    .en(En));
  Line line_1 (.EnT(T0), .Tail_X(Tail_X), .Head_X(Head_X), .Out(_0), .Smash(S0), .EnH(H0), .CLEAR(CLEAR));
  Line line_2 (.EnT(T1), .Tail_X(Tail_X), .Head_X(Head_X), .Out(out_10), .Smash(S1), .EnH(H1), .CLEAR(CLEAR));
  Line line_3 (.EnT(T2), .Tail_X(Tail_X), .Head_X(Head_X), .Out(out_11), .Smash(S2), .EnH(H2), .CLEAR(CLEAR));
  Line line_4 (.EnT(T3), .Tail_X(Tail_X), .Head_X(Head_X), .Out(out_12), .Smash(S3), .EnH(H3), .CLEAR(CLEAR));
  Line line_5 (.EnT(T4), .Tail_X(Tail_X), .Head_X(Head_X), .Out(out_13), .Smash(S4), .EnH(H4), .CLEAR(CLEAR));
  Line line_6 (.EnT(T5), .Tail_X(Tail_X), .Head_X(Head_X), .Out(out_14), .Smash(S5), .EnH(H5), .CLEAR(CLEAR));
  Line line_7 (.EnT(T6), .Tail_X(Tail_X), .Head_X(Head_X), .Out(out_15), .Smash(S6), .EnH(H6), .CLEAR(CLEAR));
  Line line_8 (.EnT(T7), .Tail_X(Tail_X), .Head_X(Head_X), .Out(out_16), .Smash(S7), .EnH(H7), .CLEAR(CLEAR));
  Line line_9 (.EnT(T8), .Tail_X(Tail_X), .Head_X(Head_X), .Out(out_17), .Smash(S8), .EnH(H8), .CLEAR(CLEAR));
  Line line_10 (.EnT(T9), .Tail_X(Tail_X), .Head_X(Head_X), .Out(out_18), .Smash(S9), .EnH(H9), .CLEAR(CLEAR));
  Line line_11 (.EnT(T10), .Tail_X(Tail_X), .Head_X(Head_X), .Out(out_19), .Smash(S10), .EnH(H10), .CLEAR(CLEAR));
  Line line_12 (.EnT(T11), .Tail_X(Tail_X), .Head_X(Head_X), .Out(out_20), .Smash(S11), .EnH(H11), .CLEAR(CLEAR));
  Line line_13 (.EnT(T12), .Tail_X(Tail_X), .Head_X(Head_X), .Out(out_21), .Smash(S12), .EnH(H12), .CLEAR(CLEAR));
  Line line_14 (.EnT(T13), .Tail_X(Tail_X), .Head_X(Head_X), .Out(out_22), .Smash(S13), .EnH(H13), .CLEAR(CLEAR));
  Line line_15 (.EnT(T14), .Tail_X(Tail_X), .Head_X(Head_X), .Out(out_23), .Smash(S14), .EnH(H14), .CLEAR(CLEAR));
  Line line_16 (.EnT(T15), .Tail_X(Tail_X), .Head_X(Head_X), .Out(out_24), .Smash(S15), .EnH(H15), .CLEAR(CLEAR));
  or or_4 (Smash, S0, S1, S2, S3, S4, S5, S6, S7, S8, S9, S10, S11, S12, S13, S14, S15, S16, S17, S18, S19, S20, S21, S22, S23, S24, S25, S26, S27, S28, S29, S30, S31);
  Line line_17 (.EnT(T16), .Tail_X(Tail_X), .Head_X(Head_X), .Out(out_25), .Smash(S16), .EnH(H16), .CLEAR(CLEAR));
  Line line_18 (.EnT(T17), .Tail_X(Tail_X), .Head_X(Head_X), .Out(out_26), .Smash(S17), .EnH(H17), .CLEAR(CLEAR));
  Line line_19 (.EnT(T18), .Tail_X(Tail_X), .Head_X(Head_X), .Out(out_27), .Smash(S18), .EnH(H18), .CLEAR(CLEAR));
  Line line_20 (.EnT(T19), .Tail_X(Tail_X), .Head_X(Head_X), .Out(out_28), .Smash(S19), .EnH(H19), .CLEAR(CLEAR));
  Line line_21 (.EnT(T20), .Tail_X(Tail_X), .Head_X(Head_X), .Out(out_29), .Smash(S20), .EnH(H20), .CLEAR(CLEAR));
  Line line_22 (.EnT(T21), .Tail_X(Tail_X), .Head_X(Head_X), .Out(out_30), .Smash(S21), .EnH(H21), .CLEAR(CLEAR));
  Line line_23 (.EnT(T22), .Tail_X(Tail_X), .Head_X(Head_X), .Out(out_31), .Smash(S22), .EnH(H22), .CLEAR(CLEAR));
  Line line_24 (.EnT(T23), .Tail_X(Tail_X), .Head_X(Head_X), .Out(out_32), .Smash(S23), .EnH(H23), .CLEAR(CLEAR));
  Line line_25 (.EnT(T24), .Tail_X(Tail_X), .Head_X(Head_X), .Out(out_33), .Smash(S24), .EnH(H24), .CLEAR(CLEAR));
  Line line_26 (.EnT(T25), .Tail_X(Tail_X), .Head_X(Head_X), .Out(out_34), .Smash(S25), .EnH(H25), .CLEAR(CLEAR));
  Line line_27 (.EnT(T26), .Tail_X(Tail_X), .Head_X(Head_X), .Out(out_35), .Smash(S26), .EnH(H26), .CLEAR(CLEAR));
  Line line_28 (.EnT(T27), .Tail_X(Tail_X), .Head_X(Head_X), .Out(out_36), .Smash(S27), .EnH(H27), .CLEAR(CLEAR));
  Line line_29 (.EnT(T28), .Tail_X(Tail_X), .Head_X(Head_X), .Out(out_37), .Smash(S28), .EnH(H28), .CLEAR(CLEAR));
  Line line_30 (.EnT(T29), .Tail_X(Tail_X), .Head_X(Head_X), .Out(out_38), .Smash(S29), .EnH(H29), .CLEAR(CLEAR));
  Line line_31 (.EnT(T30), .Tail_X(Tail_X), .Head_X(Head_X), .Out(out_39), .Smash(S30), .EnH(H30), .CLEAR(CLEAR));
  Line line_32 (.EnT(T31), .Tail_X(Tail_X), .Head_X(Head_X), .Out(out_40), .Smash(S31), .EnH(H31), .CLEAR(CLEAR));

  // Other names for the same wires on the sheet: O0[31:0] = _0; O1[31:0] = out_10; O2[31:0] = out_11;
  //   O3[31:0] = out_12; O4[31:0] = out_13; O5[31:0] = out_14; O6[31:0] = out_15; O7[31:0] = out_16;
  //   O8[31:0] = out_17; O9[31:0] = out_18; O10[31:0] = out_19; O11[31:0] = out_20; O12[31:0] = out_21;
  //   O13[31:0] = out_22; O14[31:0] = out_23; O15[31:0] = out_24; O16[31:0] = out_25; O17[31:0] = out_26;
  //   O18[31:0] = out_27; O19[31:0] = out_28; O20[31:0] = out_29; O21[31:0] = out_30; O22[31:0] = out_31;
  //   O23[31:0] = out_32; O24[31:0] = out_33; O25[31:0] = out_34; O26[31:0] = out_35; O27[31:0] = out_36;
  //   O28[31:0] = out_37; O29[31:0] = out_38; O30[31:0] = out_39; O31[31:0] = out_40
endmodule

module Line (
  input  CLEAR,
  input  EnT,
  input  EnH,
  input  [4:0] Tail_X,
  input  [4:0] Head_X,
  output [31:0] Out,
  output Smash
);

  wire H0, H1, H2, H3, H4, H5, H6, H7, H8, H9, H10, H11, H12, H13, H14, H15, H16, H17, H18, H19, H20, H21,
       H22, H23, H24, H25, H26, H27, H28, H29, H30, H31, S0, S1, S2, S3, S4, S5, S6, S7, S8, S9, S10, S11,
       S12, S13, S14, S15, S16, S17, S18, S19, S20, S21, S22, S23, S24, S25, S26, S27, S28, S29, S30, S31,
       T0, T1, T2, T3, T4, T5, T6, T7, T8, T9, T10, T11, T12, T13, T14, T15, T16, T17, T18, T19, T20, T21,
       T22, T23, T24, T25, T26, T27, T28, T29, T30, T31;

  Decoder #(.select(5), .disabled(0)) decoder_1 (
    .out0(T0), .out1(T1), .out2(T2), .out3(T3), .out4(T4), .out5(T5), .out6(T6), .out7(T7), .out8(T8),
    .out9(T9), .out10(T10), .out11(T11), .out12(T12), .out13(T13), .out14(T14), .out15(T15), .out16(T16),
    .out17(T17), .out18(T18), .out19(T19), .out20(T20), .out21(T21), .out22(T22), .out23(T23), .out24(T24),
    .out25(T25), .out26(T26), .out27(T27), .out28(T28), .out29(T29), .out30(T30), .out31(T31), .sel(Tail_X),
    .en(EnT));
  pixel pixel_1 (.Up(H0), .Down(T0), .Light(Out[31]), .Smash(S0), .CLEAR(CLEAR));
  pixel pixel_2 (.Up(H16), .Down(T16), .Light(Out[15]), .Smash(S16), .CLEAR(CLEAR));
  Decoder #(.select(5), .disabled(0)) decoder_2 (
    .out0(H0), .out1(H1), .out2(H2), .out3(H3), .out4(H4), .out5(H5), .out6(H6), .out7(H7), .out8(H8),
    .out9(H9), .out10(H10), .out11(H11), .out12(H12), .out13(H13), .out14(H14), .out15(H15), .out16(H16),
    .out17(H17), .out18(H18), .out19(H19), .out20(H20), .out21(H21), .out22(H22), .out23(H23), .out24(H24),
    .out25(H25), .out26(H26), .out27(H27), .out28(H28), .out29(H29), .out30(H30), .out31(H31), .sel(Head_X),
    .en(EnH));
  pixel pixel_3 (.Up(H1), .Down(T1), .Light(Out[30]), .Smash(S1), .CLEAR(CLEAR));
  pixel pixel_4 (.Up(H2), .Down(T2), .Light(Out[29]), .Smash(S2), .CLEAR(CLEAR));
  pixel pixel_5 (.Up(H18), .Down(T18), .Light(Out[13]), .Smash(S18), .CLEAR(CLEAR));
  pixel pixel_6 (.Up(H17), .Down(T17), .Light(Out[14]), .Smash(S17), .CLEAR(CLEAR));
  pixel pixel_7 (.Up(H3), .Down(T3), .Light(Out[28]), .Smash(S3), .CLEAR(CLEAR));
  pixel pixel_8 (.Up(H19), .Down(T19), .Light(Out[12]), .Smash(S19), .CLEAR(CLEAR));
  pixel pixel_9 (.Up(H4), .Down(T4), .Light(Out[27]), .Smash(S4), .CLEAR(CLEAR));
  pixel pixel_10 (.Up(H5), .Down(T5), .Light(Out[26]), .Smash(S5), .CLEAR(CLEAR));
  pixel pixel_11 (.Up(H20), .Down(T20), .Light(Out[11]), .Smash(S20), .CLEAR(CLEAR));
  pixel pixel_12 (.Up(H21), .Down(T21), .Light(Out[10]), .Smash(S21), .CLEAR(CLEAR));
  pixel pixel_13 (.Up(H6), .Down(T6), .Light(Out[25]), .Smash(S6), .CLEAR(CLEAR));
  pixel pixel_14 (.Up(H22), .Down(T22), .Light(Out[9]), .Smash(S22), .CLEAR(CLEAR));
  or or_1 (Smash, S0, S1, S2, S3, S4, S5, S6, S7, S8, S9, S10, S11, S12, S13, S14, S15, S16, S17, S18, S19, S20, S21, S22, S23, S24, S25, S26, S27, S28, S29, S30, S31);
  pixel pixel_15 (.Up(H8), .Down(T8), .Light(Out[23]), .Smash(S8), .CLEAR(CLEAR));
  pixel pixel_16 (.Up(H7), .Down(T7), .Light(Out[24]), .Smash(S7), .CLEAR(CLEAR));
  pixel pixel_17 (.Up(H23), .Down(T23), .Light(Out[8]), .Smash(S23), .CLEAR(CLEAR));
  pixel pixel_18 (.Up(H24), .Down(T24), .Light(Out[7]), .Smash(S24), .CLEAR(CLEAR));
  pixel pixel_19 (.Up(H9), .Down(T9), .Light(Out[22]), .Smash(S9), .CLEAR(CLEAR));
  pixel pixel_20 (.Up(H10), .Down(T10), .Light(Out[21]), .Smash(S10), .CLEAR(CLEAR));
  pixel pixel_21 (.Up(H26), .Down(T26), .Light(Out[5]), .Smash(S26), .CLEAR(CLEAR));
  pixel pixel_22 (.Up(H25), .Down(T25), .Light(Out[6]), .Smash(S25), .CLEAR(CLEAR));
  pixel pixel_23 (.Up(H11), .Down(T11), .Light(Out[20]), .Smash(S11), .CLEAR(CLEAR));
  pixel pixel_24 (.Up(H27), .Down(T27), .Light(Out[4]), .Smash(S27), .CLEAR(CLEAR));
  pixel pixel_25 (.Up(H13), .Down(T13), .Light(Out[18]), .Smash(S13), .CLEAR(CLEAR));
  pixel pixel_26 (.Up(H12), .Down(T12), .Light(Out[19]), .Smash(S12), .CLEAR(CLEAR));
  pixel pixel_27 (.Up(H29), .Down(T29), .Light(Out[2]), .Smash(S29), .CLEAR(CLEAR));
  pixel pixel_28 (.Up(H28), .Down(T28), .Light(Out[3]), .Smash(S28), .CLEAR(CLEAR));
  pixel pixel_29 (.Up(H14), .Down(T14), .Light(Out[17]), .Smash(S14), .CLEAR(CLEAR));
  pixel pixel_30 (.Up(H30), .Down(T30), .Light(Out[1]), .Smash(S30), .CLEAR(CLEAR));
  pixel pixel_31 (.Up(H15), .Down(T15), .Light(Out[16]), .Smash(S15), .CLEAR(CLEAR));
  pixel pixel_32 (.Up(H31), .Down(T31), .Light(Out[0]), .Smash(S31), .CLEAR(CLEAR));

  // Other names for the same wires on the sheet: L31 = Out[0]; L30 = Out[1]; L29 = Out[2]; L28 = Out[3]; L27 = Out[4];
  //   L26 = Out[5]; L25 = Out[6]; L24 = Out[7]; L23 = Out[8]; L22 = Out[9]; L21 = Out[10]; L20 = Out[11];
  //   L19 = Out[12]; L18 = Out[13]; L17 = Out[14]; L16 = Out[15]; L15 = Out[16]; L14 = Out[17]; L13 = Out[18];
  //   L12 = Out[19]; L11 = Out[20]; L10 = Out[21]; L9 = Out[22]; L8 = Out[23]; L7 = Out[24]; L6 = Out[25];
  //   L5 = Out[26]; L4 = Out[27]; L3 = Out[28]; L2 = Out[29]; L1 = Out[30]; L0 = Out[31]
endmodule

module pixel (
  input  CLEAR,
  input  Up,
  input  Down,
  output Light,
  output Smash
);

  wire and_1_out, or_1_out, Visited;

  D_Flip_Flop d_ff_1 (.clk(Up), .D(1'b1), .Q(Light), .reset(or_1_out));  // open: Qn, preset, en
  and and_1 (and_1_out, ~Up, Down);  // AND_Gate
  and and_2 (Smash, Visited, Up);
  or or_1 (or_1_out, and_1_out, CLEAR);
  D_Flip_Flop #(.trigger("falling")) d_ff_2 (
    .clk(Up), .D(1'b1), .Q(Visited), .reset(or_1_out));  // open: Qn, preset, en
endmodule

module Keyboard (
  input  GameClock,
  input  Turn,
  input  START,
  input  [6:0] In,
  output Pause,
  output [1:0] Where,
  output D,
  output W,
  output S,
  output A
);

  wire and_1_out, bitshrink_1_pause, pull_resistor_1_node;

  bitShrink bitshrink_1 (.In(In), .W(W), .A(A), .S(S), .D(D), .Where(Where), .Pause(bitshrink_1_pause));
  and and_1 (and_1_out, ~GameClock, bitshrink_1_pause);  // AND_Gate
  D_Flip_Flop d_ff_1 (.clk(and_1_out), .D(pull_resistor_1_node), .Q(Pause), .reset(START));  // open: Qn, preset, en
  Pull_Resistor #(.pull(1)) pull_resistor_1 (.node(pull_resistor_1_node));
  assign pull_resistor_1_node = bitshrink_1_pause ? ~bitshrink_1_pause : 1'bz;  // Controlled_Inverter controlled_inverter_1
endmodule

module bitShrink (
  input  [6:0] In,
  output W,
  output A,
  output [1:0] Where,
  output S,
  output D,
  output Pause
);

  wire [6:0] xnor_1_out, xnor_2_out, xnor_3_out, xnor_4_out, xnor_5_out;

  // Probe on 7'b1110111
  // Probe on 7'b1100001
  // Probe on 7'b1110011
  // Probe on 7'b1100100
  // Probe on 7'b0100000
  assign xnor_1_out = ~(In ^ 7'b1110111);  // XNOR_Gate xnor_1, 7 bits wide
  assign xnor_2_out = ~(In ^ 7'b1100001);  // XNOR_Gate xnor_2, 7 bits wide
  assign xnor_3_out = ~(In ^ 7'b1110011);  // XNOR_Gate xnor_3, 7 bits wide
  assign xnor_4_out = ~(In ^ 7'b1100100);  // XNOR_Gate xnor_4, 7 bits wide
  assign xnor_5_out = ~(In ^ 7'b0100000);  // XNOR_Gate xnor_5, 7 bits wide
  and and_1 (W, xnor_1_out[0], xnor_1_out[1], xnor_1_out[2], xnor_1_out[3], xnor_1_out[4], xnor_1_out[5], xnor_1_out[6]);
  and and_2 (A, xnor_2_out[0], xnor_2_out[1], xnor_2_out[2], xnor_2_out[3], xnor_2_out[4], xnor_2_out[5], xnor_2_out[6]);
  and and_3 (S, xnor_3_out[0], xnor_3_out[1], xnor_3_out[2], xnor_3_out[3], xnor_3_out[4], xnor_3_out[5], xnor_3_out[6]);
  and and_4 (D, xnor_4_out[0], xnor_4_out[1], xnor_4_out[2], xnor_4_out[3], xnor_4_out[4], xnor_4_out[5], xnor_4_out[6]);
  and and_5 (Pause, xnor_5_out[0], xnor_5_out[1], xnor_5_out[2], xnor_5_out[3], xnor_5_out[4], xnor_5_out[5], xnor_5_out[6]);
  assign Where = W ? 2'b00 : 2'bz;  // Controlled_Buffer controlled_buffer_1
  assign Where = A ? 2'b01 : 2'bz;  // Controlled_Buffer controlled_buffer_2
  assign Where = S ? 2'b10 : 2'bz;  // Controlled_Buffer controlled_buffer_3
  assign Where = D ? 2'b11 : 2'bz;  // Controlled_Buffer controlled_buffer_4
  Pull_Resistor pull_resistor_1 (.node(Where));
endmodule

module Apples (
  input  [31:0] L1,
  input  [31:0] L1_2
);

  wire or_1_out;
  wire [4:0] random_1_out, random_2_out;
  wire [31:0] and_1_out, multiplexer_1_out, shifter_1_out;

  Random #(.width(5)) random_1 (.clk(or_1_out), .out(random_1_out));  // open: next, clr
  Random #(.width(5)) random_2 (.clk(or_1_out), .out(random_2_out));  // open: next, clr
  Multiplexer #(.select(5), .width(32)) multiplexer_1 (
    .out(multiplexer_1_out), .sel(random_1_out));  // open: in0, in1, in2, in3, in4, in5, in6, in7, in8, in9, in10, in11, in12, in13, in14, in15, in16, in17, in18, in19, in20, in21, in22, in23, in24, in25, in26, in27, in28, in29, in30, in31, en
  Shifter #(.width(32)) shifter_1 (.in(32'h1), .\dist (random_2_out), .out(shifter_1_out));
  assign and_1_out = shifter_1_out & multiplexer_1_out;  // AND_Gate and_1, 32 bits wide
  or or_1 (or_1_out, and_1_out[0], and_1_out[1], and_1_out[2], and_1_out[3], and_1_out[4], and_1_out[5], and_1_out[6], and_1_out[7], and_1_out[8], and_1_out[9], and_1_out[10], and_1_out[11], and_1_out[12], and_1_out[13], and_1_out[14], and_1_out[15], and_1_out[16], and_1_out[17], and_1_out[18], and_1_out[19], and_1_out[20], and_1_out[21], and_1_out[22], and_1_out[23], and_1_out[24], and_1_out[25], and_1_out[26], and_1_out[27], and_1_out[28], and_1_out[29], and_1_out[30], and_1_out[31]);
endmodule

module Inc (
  input  [5:0] in,
  input  En,
  output [5:0] out
);

  wire not_1_out;
  wire [5:0] xor_1_out;
  wire [5:1] and_1_out;
  wire [5:5] and_1_out_2;

  // Probe on in
  assign {and_1_out_2[5], and_1_out} = in & {and_1_out, 1'b1};  // AND_Gate and_1, 6 bits wide
  assign xor_1_out = {and_1_out, 1'b1} ^ in;  // XOR_Gate xor_1, 6 bits wide
  // Probe on xor_1_out
  Multiplexer #(.width(6), .enable("false")) multiplexer_1 (.in0(xor_1_out), .in1(in), .out(out), .sel(not_1_out));
  not not_1 (not_1_out, En);
endmodule

module test (
  input  [1:0] EnT
);

  wire clock_1_out;
  wire [31:0] map_loader_1_p3, map_loader_1_p4, map_loader_1_p5, map_loader_1_p6, map_loader_1_p7,
       map_loader_1_p8, map_loader_1_p9, map_loader_1_p10, map_loader_1_p11, map_loader_1_p12,
       map_loader_1_p13, map_loader_1_p14, map_loader_1_p15, map_loader_1_p16, map_loader_1_p17,
       map_loader_1_p18, map_loader_1_p19, map_loader_1_p20, map_loader_1_p21, map_loader_1_p22,
       map_loader_1_p23, map_loader_1_p24, map_loader_1_p25, map_loader_1_p26, map_loader_1_p27,
       map_loader_1_p28, map_loader_1_p29, map_loader_1_p30, map_loader_1_p31, map_loader_1_p32,
       map_loader_1_p33, map_loader_1_p34;

  Clock clock_1 (.out(clock_1_out));
  DotMatrix #(.inputtype("row"), .matrixcols(32), .matrixrows(32)) dotmatrix_1 (
    .row0(map_loader_1_p3), .row1(map_loader_1_p4), .row2(map_loader_1_p5), .row3(map_loader_1_p6),
    .row4(map_loader_1_p7), .row5(map_loader_1_p8), .row6(map_loader_1_p9), .row7(map_loader_1_p10),
    .row8(map_loader_1_p11), .row9(map_loader_1_p12), .row10(map_loader_1_p13), .row11(map_loader_1_p14),
    .row12(map_loader_1_p15), .row13(map_loader_1_p16), .row14(map_loader_1_p17), .row15(map_loader_1_p18),
    .row16(map_loader_1_p19), .row17(map_loader_1_p20), .row18(map_loader_1_p21), .row19(map_loader_1_p22),
    .row20(map_loader_1_p23), .row21(map_loader_1_p24), .row22(map_loader_1_p25), .row23(map_loader_1_p26),
    .row24(map_loader_1_p27), .row25(map_loader_1_p28), .row26(map_loader_1_p29), .row27(map_loader_1_p30),
    .row28(map_loader_1_p31), .row29(map_loader_1_p32), .row30(map_loader_1_p33), .row31(map_loader_1_p34));
  // map_loader map_loader_1: pin names not known; wires that end beside it: EnT, clock_1_out, map_loader_1_p3, map_loader_1_p4, map_loader_1_p5, map_loader_1_p6, map_loader_1_p7, map_loader_1_p8, map_loader_1_p9, map_loader_1_p10, map_loader_1_p11, map_loader_1_p12, map_loader_1_p13, map_loader_1_p14, map_loader_1_p15, map_loader_1_p16, map_loader_1_p17, map_loader_1_p18, map_loader_1_p19, map_loader_1_p20, map_loader_1_p21, map_loader_1_p22, map_loader_1_p23, map_loader_1_p24, map_loader_1_p25, map_loader_1_p26, map_loader_1_p27, map_loader_1_p28, map_loader_1_p29, map_loader_1_p30, map_loader_1_p31, map_loader_1_p32, map_loader_1_p33, map_loader_1_p34
endmodule
