// Logisim project map_circus.circ as structural Verilog: 1 circuit, main circuit main
module main (
  output [31:0] bebra
);

  wire active_reg1, active_reg2, active_reg3, active_reg4, active_reg5, active_reg6, active_reg7,
       active_reg8, active_reg9, active_reg10, active_reg11, active_reg12, active_reg13, active_reg14,
       active_reg15, active_reg16, active_reg17, active_reg18, active_reg19, active_reg20, active_reg21,
       active_reg22, active_reg23, active_reg24, active_reg25, active_reg26, active_reg27, active_reg28,
       active_reg29, active_reg30, active_reg31, active_reg32, gen2maps, power_map_1, power_map_2,
       power_map_3, power_map_4;
  wire [1:0] register_1_q;
  wire [4:0] reg_adr;
  wire [31:0] from_reg1, from_reg2, from_reg3, from_reg4, from_reg5, from_reg6, from_reg7, from_reg8,
       from_reg9, from_reg10, from_reg11, from_reg12, from_reg13, from_reg14, from_reg15, from_reg16,
       from_reg17, from_reg18, from_reg19, from_reg20, from_reg21, from_reg22, from_reg23, from_reg24,
       from_reg25, from_reg26, from_reg27, from_reg28, from_reg29, from_reg30, from_reg31, from_reg32,
       rom_1_data, to_reg1, to_reg2, to_reg3, to_reg4, to_reg5, to_reg6, to_reg7, to_reg8, to_reg9, to_reg10,
       to_reg11, to_reg12, to_reg13, to_reg14, to_reg15, to_reg16, to_reg17, to_reg18, to_reg19, to_reg20,
       to_reg21, to_reg22, to_reg23, to_reg24, to_reg25, to_reg26, to_reg27, to_reg28, to_reg29, to_reg30,
       to_reg31, to_reg32;

  Register #(.width(32), .trigger("falling")) map_reg1 (
    .D(to_reg1), .Q(from_reg1), .clk(active_reg1));  // open: en, clr
  Register #(.width(32), .trigger("falling")) map_reg2 (
    .D(to_reg2), .Q(from_reg2), .clk(active_reg2));  // open: en, clr
  Register #(.width(32), .trigger("falling")) reg3 (.D(to_reg3), .Q(from_reg3), .clk(active_reg3));  // open: en, clr
  Register #(.width(32), .trigger("falling")) reg4 (.D(to_reg4), .Q(from_reg4), .clk(active_reg4));  // open: en, clr
  Decoder #(.select(5), .disabled(0), .enable("false")) decoder_1 (
    .out0(active_reg1), .out1(active_reg2), .out2(active_reg3), .out3(active_reg4), .out4(active_reg5),
    .out5(active_reg6), .out6(active_reg7), .out7(active_reg8), .out8(active_reg9), .out9(active_reg10),
    .out10(active_reg11), .out11(active_reg12), .out12(active_reg13), .out13(active_reg14),
    .out14(active_reg15), .out15(active_reg16), .out16(active_reg17), .out17(active_reg18),
    .out18(active_reg19), .out19(active_reg20), .out20(active_reg21), .out21(active_reg22),
    .out22(active_reg23), .out23(active_reg24), .out24(active_reg25), .out25(active_reg26),
    .out26(active_reg27), .out27(active_reg28), .out28(active_reg29), .out29(active_reg30),
    .out30(active_reg31), .out31(active_reg32), .sel(reg_adr));
  Register #(.width(32), .trigger("falling")) reg5 (.D(to_reg5), .Q(from_reg5), .clk(active_reg5));  // open: en, clr
  Register #(.width(32), .trigger("falling")) reg6 (.D(to_reg6), .Q(from_reg6), .clk(active_reg6));  // open: en, clr
  Register #(.width(32), .trigger("falling")) reg7 (.D(to_reg7), .Q(from_reg7), .clk(active_reg7));  // open: en, clr
  Register #(.width(32), .trigger("falling")) reg8 (.D(to_reg8), .Q(from_reg8), .clk(active_reg8));  // open: en, clr
  Register #(.width(32), .trigger("falling")) reg9 (.D(to_reg9), .Q(from_reg9), .clk(active_reg9));  // open: en, clr
  Register #(.width(32), .trigger("falling")) reg10 (
    .D(to_reg10), .Q(from_reg10), .clk(active_reg10));  // open: en, clr
  Register #(.width(32), .trigger("falling")) reg11 (
    .D(to_reg11), .Q(from_reg11), .clk(active_reg11));  // open: en, clr
  Register #(.width(32), .trigger("falling")) reg12 (
    .D(to_reg12), .Q(from_reg12), .clk(active_reg12));  // open: en, clr
  Counter #(.width(5), .max('h1f)) counter_1 (.Q(reg_adr), .clk(gen2maps));  // open: load, D, count, carry, clr
  Register #(.width(32), .trigger("falling")) reg13 (
    .D(to_reg13), .Q(from_reg13), .clk(active_reg13));  // open: en, clr
  Register #(.width(32), .trigger("falling")) reg14 (
    .D(to_reg14), .Q(from_reg14), .clk(active_reg14));  // open: en, clr
  Register #(.width(32), .trigger("falling")) reg15 (
    .D(to_reg15), .Q(from_reg15), .clk(active_reg15));  // open: en, clr
  Register #(.width(32), .trigger("falling")) reg16 (
    .D(to_reg16), .Q(from_reg16), .clk(active_reg16));  // open: en, clr
  ROM #(.addrWidth(5), .dataWidth(32)) rom_1 (.addr(reg_adr), .data(rom_1_data), .sel(power_map_1));
  ROM #(.addrWidth(5), .dataWidth(32)) rom_2 (.addr(reg_adr), .data(rom_1_data), .sel(power_map_2));
  ROM #(.addrWidth(5), .dataWidth(32)) rom_3 (.addr(reg_adr), .data(rom_1_data), .sel(power_map_3));
  ROM #(.addrWidth(5), .dataWidth(32)) rom_4 (.addr(reg_adr), .data(rom_1_data), .sel(power_map_4));
  Demultiplexer #(.select(5), .width(32), .disabled(0), .enable("false")) demultiplexer_1 (
    .out0(to_reg1), .out1(to_reg2), .out2(to_reg3), .out3(to_reg4), .out4(to_reg5), .out5(to_reg6),
    .out6(to_reg7), .out7(to_reg8), .out8(to_reg9), .out9(to_reg10), .out10(to_reg11), .out11(to_reg12),
    .out12(to_reg13), .out13(to_reg14), .out14(to_reg15), .out15(to_reg16), .out16(to_reg17),
    .out17(to_reg18), .out18(to_reg19), .out19(to_reg20), .out20(to_reg21), .out21(to_reg22),
    .out22(to_reg23), .out23(to_reg24), .out24(to_reg25), .out25(to_reg26), .out26(to_reg27),
    .out27(to_reg28), .out28(to_reg29), .out29(to_reg30), .out30(to_reg31), .out31(to_reg32),
    .in(rom_1_data), .sel(reg_adr));
  Register #(.width(32), .trigger("falling")) reg17 (
    .D(to_reg17), .Q(from_reg17), .clk(active_reg17));  // open: en, clr
  Register #(.width(32), .trigger("falling")) reg18 (
    .D(to_reg18), .Q(from_reg18), .clk(active_reg18));  // open: en, clr
  Register #(.width(32), .trigger("falling")) reg19 (
    .D(to_reg19), .Q(from_reg19), .clk(active_reg19));  // open: en, clr
  Register #(.width(32), .trigger("falling")) reg20 (
    .D(to_reg20), .Q(from_reg20), .clk(active_reg20));  // open: en, clr
  Register #(.width(32), .trigger("falling")) reg21 (
    .D(to_reg21), .Q(from_reg21), .clk(active_reg21));  // open: en, clr
  Register #(.width(32), .trigger("falling")) reg22 (
    .D(to_reg22), .Q(from_reg22), .clk(active_reg22));  // open: en, clr
  Register #(.width(32), .trigger("falling")) reg23 (
    .D(to_reg23), .Q(from_reg23), .clk(active_reg23));  // open: en, clr
  Register #(.width(32), .trigger("falling")) reg24 (
    .D(to_reg24), .Q(from_reg24), .clk(active_reg24));  // open: en, clr
  Register #(.width(2), .trigger("falling")) register_1 (.Q(register_1_q));  // open: D, en, clk, clr
  Decoder #(.select(2), .enable("false")) decoder_2 (
    .out0(power_map_1), .out1(power_map_2), .out2(power_map_3), .out3(power_map_4), .sel(register_1_q));
  Register #(.width(32), .trigger("falling")) reg25 (
    .D(to_reg25), .Q(from_reg25), .clk(active_reg25));  // open: en, clr
  Register #(.width(32), .trigger("falling")) reg26 (
    .D(to_reg26), .Q(from_reg26), .clk(active_reg26));  // open: en, clr
  Register #(.width(32), .trigger("falling")) reg27 (
    .D(to_reg27), .Q(from_reg27), .clk(active_reg27));  // open: en, clr
  Register #(.width(32), .trigger("falling")) reg28 (
    .D(to_reg28), .Q(from_reg28), .clk(active_reg28));  // open: en, clr
  Register #(.width(32), .trigger("falling")) reg29 (
    .D(to_reg29), .Q(from_reg29), .clk(active_reg29));  // open: en, clr
  Register #(.width(32), .trigger("falling")) reg30 (
    .D(to_reg30), .Q(from_reg30), .clk(active_reg30));  // open: en, clr
  Register #(.width(32), .trigger("falling")) reg31 (
    .D(to_reg31), .Q(from_reg31), .clk(active_reg31));  // open: en, clr
  Register #(.width(32), .trigger("falling")) reg32 (
    .D(to_reg32), .Q(from_reg32), .clk(active_reg32));  // open: en, clr
  // also tied to GND on the sheet: {register_1_q[0], register_1_q[1]}

  // Notes on the sheet:
  //   contents of rom_1 (hex, n*v repeats v):
  //   11111111 11111111 11111111 8*0 1111111 18*0 11111111 11111111
  //   contents of rom_2 (hex, n*v repeats v):
  //   28*0 123 0 0 123
endmodule
